# Fritzing sketch plotter_head (saved by Fritzing 0.9.0b)
circuit board: 6.99757cm x 5.46765cm

parts:
  5Vto3V = Logic Level Converter
  BTM-112 = BTM-112
  J1 = male pin header, 3 pins [form="♂ (male)"]
  J2 = male pin header, 3 pins [form="♂ (male)"]
  J3 = male pin header, 3 pins [form="♂ (male)"]
  LED1 = LED - 3mm [color="Red (633nm)" package="3 mm [THT]"]
  LED2 = LED - 3mm [color="Green (565nm)" package="3 mm [THT]"]
  R5 = Resistor [tolerance=±5% resistance=220 package=THT]
  R6 = Resistor [tolerance=±5% resistance=220 package=THT]
  CONN1 = SMA-15
  Part1 = Arduino Uno (Rev3)
  J3B = male pin header, 3 pins [form="♂ (male)"]
  J2B = male pin header, 3 pins [form="♂ (male)"]
  J1B = male pin header, 3 pins [form="♂ (male)"]

nets:
  GND: 5Vto3V.GND, BTM-112.GND, J1.pin1, J2.pin1, J3.pin1, LED1.cathode, LED2.cathode, CONN1.GND, Part1.GND, J3B.pin1, J2B.pin1, J1B.pin1
  3V3: 5Vto3V.LV, BTM-112.3V3, Part1.3V3
  N1: 5Vto3V.RX_LV, BTM-112.UART_TX
  N2: 5Vto3V.TX_LV, BTM-112.UART_RX
  N3: 5Vto3V.TX_HV, Part1.D3_PWM
  N4: 5Vto3V.RX_HV, Part1.D2
  N5: 5Vto3V.HV, J1.pin2, J2.pin2, J3.pin2, Part1.5V, J3B.pin2, J2B.pin2, J1B.pin2
  N6: BTM-112.PIO7, R5.Pin_0
  N7: BTM-112.PIO6, R6.Pin_0
  N8: BTM-112.RF_IO, CONN1.SIGNAL
  N9: J1.pin3, Part1.D9_PWM, J1B.pin3
  N10: J2.pin3, Part1.D11_PWM/MOSI, J2B.pin3
  N11: J3.pin3, Part1.D10_PWM/SS, J3B.pin3
  N12: LED1.anode, R5.Pin_1
  N13: LED2.anode, R6.Pin_1

notes:
  plotter head v1.1

custom parts:
  BTM-112: Bluetooth SMD module
  SMA-15: SMA 15 connector
